// Logisim project lab11A.circ as structural Verilog
module main (
  output [15:0] Instruction,
  output [7:0] Immediate,
  output Register,
  output [3:0] Opcode,
  output [7:0] RegisterWriteData,
  output [7:0] Register0,
  output [7:0] Register1,
  output [7:0] ALUResult
);

  wire add, clk, \nand , \nor , not_1_out, set, sub;
  wire [1:0] ALUOp;
  wire [7:0] adder_1_out, register_1_q;

  Register register_1 (.D(adder_1_out), .en(1'b1), .Q(register_1_q), .clk(clk));  // open: clr
  Clock clock_1 (.out(clk));
  Adder adder_1 (.a(register_1_q), .b(8'h1), .out(adder_1_out));  // open: cin, cout
  Decoder #(.select(4)) decoder_1 (
    .out0(set), .out4(add), .out5(sub), .out8(\nor ), .out9(\nand ), .sel(Instruction[15:12]));  // open: out1, out2, out3, out6, out7, out10, out11, out12, out13, out14, out15, en
  ROM #(.dataWidth(16)) rom_1 (.addr(register_1_q), .data({Instruction[15:8], Immediate}), .sel(1'b1));
  Priority_Encoder #(.select(2)) priority_encoder_1 (
    .in0(1'b1), .in1(sub), .in2(\nand ), .in3(\nor ), .out(ALUOp));  // open: gs, en_out, en_in
  not not_1 (not_1_out, Instruction[11]);
  Register A (.D(RegisterWriteData), .en(not_1_out), .Q(Register0), .clk(clk));  // open: clr
  Register B (.D(RegisterWriteData), .en(Instruction[11]), .Q(Register1), .clk(clk));  // open: clr
  ALU alu_1 (.A(Register0), .B(Register1), .Operation(ALUOp), .Result(ALUResult));
  Multiplexer #(.width(8)) multiplexer_1 (
    .in0(ALUResult), .in1(Immediate), .out(RegisterWriteData), .sel(set));  // open: en

  assign Instruction[7:0] = Immediate;
  assign Opcode = Instruction[15:12];
  assign Register = Instruction[11];

  // Notes on the sheet:
  //   contents of rom_1 (hex, n*v repeats v):
  //   1 802
endmodule

module ALU (
  input  [7:0] A,
  input  [7:0] B,
  input  [1:0] Operation,
  output [7:0] Result
);

  wire [7:0] adder_1_out, nand_1_out, nor_1_out, subtractor_1_out;

  Adder adder_1 (.a(A), .b(B), .out(adder_1_out));  // open: cin, cout
  Subtractor subtractor_1 (.a(A), .b(B), .out(subtractor_1_out));  // open: bin, bout
  assign nand_1_out = ~(A & B);  // NAND_Gate nand_1, 8 bits wide
  assign nor_1_out = ~(A | B);  // NOR_Gate nor_1, 8 bits wide
  Multiplexer #(.select(2), .width(8)) multiplexer_1 (
    .in0(adder_1_out), .in1(subtractor_1_out), .in2(nand_1_out), .in3(nor_1_out), .out(Result),
    .sel(Operation));  // open: en
endmodule
