// Logisim project lab11B.circ as structural Verilog: 1 circuit, main circuit main
module main (
  input  clear,
  output sel,
  output ld,
  output [3:0] address,
  output [3:0] data
);

  wire clock_1_out, nen;
  wire [3:0] counter_1_q, counter_2_q;

  Counter #(.width(4), .max('hf), .ongoal("stay")) counter_1 (
    .Q(counter_1_q), .clk(clock_1_out), .clr(clear));  // open: load, D, count, carry
  assign address = sel ? counter_1_q : 4'bz;  // Controlled_Buffer controlled_buffer_1
  Comparator #(.width(4)) comparator_1 (.a(counter_1_q), .b(4'b1111), .eq(nen));  // open: gt, lt
  Clock clock_1 (.out(clock_1_out));
  assign data = sel ? counter_2_q : 4'bz;  // Controlled_Buffer controlled_buffer_2
  RAM #(.addrWidth(4), .dataWidth(4)) ram_1 (
    .addr(address), .data(data), .sel(sel), .clk(clock_1_out), .ld(ld), .clr(clear));
  Register #(.width(1)) register_1 (.D(nen), .en(nen), .Q(ld), .clk(clock_1_out));  // open: clr
  Counter #(.width(4), .max('hf)) counter_2 (
    .Q(counter_2_q), .clk(clock_1_out), .clr(clear));  // open: load, D, count, carry
  not not_1 (sel, ld);

  // Other names for the same wires on the sheet: clr = clear

  // Notes on the sheet:
  //   These are the inputs
  //   of your circuit.
  //   Do not modify this!
  //   Put your name and id here: Luis Oliveira - lun8
  //   These are the outputs
  //   of your circuit.
  //   Do not modify this!
endmodule
